# Fritzing sketch Display-I2C-8x2LCD (saved by Fritzing 0.7.12b)
breadboards: 1

parts:
  J2 = female pin header, 5 pins [form="♀ (female)"]
  CE_DC = female pin header, 2 pins [form="♀ (female)"]  # not connected
  LCD1 = LCD screen
  R1 = Trimmer Potentiometer [maximum_resistance=10kΩ package=THT]
  IC1 = SO18W [chip_label=IC package=SO(w)]  # not connected

nets:
  N1: J2.pin1, LCD1.VSS, R1.leg1
  N2: J2.pin2, LCD1.VDD, R1.leg2

notes:
  Clixx.io
  - + c r i
