# Fritzing sketch power-mosfet-n (saved by Fritzing 0.8.0b)
breadboards: 1

parts:
  o_i = female pin header, 2 pins [form="♀ (female)"]
  +_- = female pin header, 2 pins [form="♀ (female)"]
  Q1 = Basic FET N-Channel [package="DPak [SMD]"]
  D1 = Rectifier Diode [part_number=1N4001 package="Melf DO-213 AB [SMD]"]
  R2 = Resistor [tolerance=±5% resistance=220 package="0805 [SMD]"]
  -_+ = screw terminal, 4 pins
  R1 = Resistor [tolerance=±5% resistance=220 package="0805 [SMD]"]
  +Source = female pin header, 3 pins [form="♀ (female)"]

nets:
  N1: o_i.pin2, R2.Pin_0
  N2: +_-.pin1, +Source.pin1
  GND: +_-.pin2, Q1.source, D1.cathode, -_+.pin3, R1.Pin_0
  N3: Q1.Gate, R2.Pin_1, R1.Pin_1
  N4: Q1.drain, D1.anode, -_+.pin2
  N5: -_+.pin1, +Source.pin2
  N6: -_+.pin4, +Source.pin3

notes:
  Input <<
  r0.2
  Motor >>
  Power <<
  - +
