# Fritzing sketch power-voltmeter (saved by Fritzing 0.8.0b)
breadboards: 1

parts:
  i_o = female pin header, 2 pins [form="♀ (female)"]
  + = Pad [width=1 height=3 connect=center]
  - = Pad [width=1 height=3 connect=center]
  i = Pad [width=1 height=3 connect=center]
  +_- = female pin header, 2 pins [form="♀ (female)"]
  o = Pad [width=1 height=3 connect=center]
  J1 = female pin header, 3 pins [form="♀ (female)"]
  S1 = Toggle Switch [package=THT]

nets:
  N1: i_o.pin1, S1.L1
  N2: i_o.pin2, o.pad
  N3: +.pad, +_-.pin1, J1.pin2, S1.L2
  GND: -.pad, i.pad, +_-.pin2, J1.pin3
  N4: J1.pin1, S1.COM

notes:
  r0.1
  Voltmeter
